// Logisim project CPU.circ as structural Verilog: 1 circuit, main circuit main
module main (
  input  in_1,
  output [7:0] out_2,
  output [7:0] out_3,
  output [7:0] out_4
);

  wire and_1_out, and_2_out, and_3_out, and_4_out, and_5_out, and_6_out, and_7_out, and_8_out, clock_1_out,
       d_ff_1_qn, decoder_1_out0, decoder_1_out1, decoder_1_out2, decoder_1_out3, Instruction_Clock_out,
       nand_1_out, not_1_out, not_2_out, not_3_out;
  wire [7:0] adder_1_out, adder_2_out, Data_dout, multiplexer_1_out, multiplexer_2_out, multiplexer_3_out,
       multiplexer_4_out, PC_q, subtractor_1_out, X0_q, X1_q, X2_q, X3_q;

  Clock #(.highDuration(2), .lowDuration(2)) Instruction_Clock (.out(Instruction_Clock_out));
  Register PC (.D(adder_1_out), .clk(Instruction_Clock_out), .Q(PC_q));  // open: en, clr
  Adder adder_1 (.a(8'h1), .b(PC_q), .out(adder_1_out));  // open: cin, cout
  RAM Instructions (.addr(PC_q), .we(in_1), .oe(1'b1), .clk(Instruction_Clock_out), .dout(out_2));  // open: din
  not not_1 (not_1_out, Instruction_Clock_out);
  Decoder #(.select(2)) decoder_1 (
    .out0(decoder_1_out0), .out1(decoder_1_out1), .out2(decoder_1_out2), .out3(decoder_1_out3),
    .sel(out_2[5:4]));  // open: en
  nand nand_1 (nand_1_out, out_2[7], out_2[6]);
  not not_2 (not_2_out, not_1_out);
  and and_1 (and_1_out, Instruction_Clock_out, not_3_out);
  not not_3 (not_3_out, not_2_out);
  and and_2 (and_2_out, nand_1_out, decoder_1_out0);
  D_Flip_Flop d_ff_1 (.D(1'b1), .clk(Instruction_Clock_out), .Qn(d_ff_1_qn));  // open: Q, preset, reset
  and and_3 (and_3_out, nand_1_out, decoder_1_out1);
  and and_4 (and_4_out, nand_1_out, decoder_1_out2);
  and and_5 (and_5_out, nand_1_out, decoder_1_out3);
  Register X0 (.D(out_4), .en(and_2_out), .clk(and_1_out), .Q(X0_q), .clr(d_ff_1_qn));
  Register X1 (.D(out_4), .en(and_3_out), .clk(and_1_out), .Q(X1_q), .clr(d_ff_1_qn));
  Register X2 (.D(out_4), .en(and_4_out), .clk(and_1_out), .Q(X2_q), .clr(d_ff_1_qn));
  Register X3 (.D(out_4), .en(and_5_out), .clk(and_1_out), .Q(X3_q), .clr(d_ff_1_qn));
  Multiplexer #(.select(2), .width(8)) multiplexer_1 (
    .in0(X0_q), .in1(X1_q), .in2(X2_q), .in3(X3_q), .out(multiplexer_1_out), .sel(out_2[3:2]));
  Multiplexer #(.select(2), .width(8)) multiplexer_2 (
    .in0(X0_q), .in1(X1_q), .in2(X2_q), .in3(X3_q), .out(multiplexer_2_out), .sel(out_2[1:0]));
  Multiplexer #(.select(2), .width(8)) multiplexer_3 (
    .in0(X0_q), .in1(X1_q), .in2(X2_q), .in3(X3_q), .out(multiplexer_3_out), .sel(out_2[5:4]));
  Adder adder_2 (.a(multiplexer_1_out), .b(multiplexer_2_out), .out(adder_2_out));  // open: cin, cout
  Subtractor subtractor_1 (.a(multiplexer_1_out), .b(multiplexer_2_out), .out(subtractor_1_out));  // open: bin, bout
  Hex_Digit_Display hex_digit_display_1 (.value(out_4[7:4]));  // open: dp
  Hex_Digit_Display hex_digit_display_2 (.value(out_4[3:0]));  // open: dp
  and and_6 (and_6_out, out_2[7], ~out_2[6]);  // AND_Gate
  Multiplexer #(.width(8)) multiplexer_4 (
    .in0(adder_2_out), .in1(subtractor_1_out), .out(multiplexer_4_out), .sel(and_6_out));
  and and_7 (and_7_out, ~out_2[7], out_2[6]);  // AND_Gate
  and and_8 (and_8_out, out_2[6], out_2[7]);
  Clock clock_1 (.out(clock_1_out));
  RAM Data (
    .addr(multiplexer_4_out), .we(and_8_out), .oe(and_7_out), .clk(clock_1_out), .din(multiplexer_3_out),
    .dout(Data_dout));
  Multiplexer #(.width(8)) multiplexer_5 (.in0(multiplexer_4_out), .in1(Data_dout), .out(out_4), .sel(and_7_out));

  assign out_3 = out_2;

  // Notes on the sheet:
  //   PC Incrementer
  //   Stage 1: IF
  //   WriteReg
  //   WriteReg
  //   Stage 5: Write Back
  //   I (instruction)
  //   ADD / SUB
  //   WriteReg
  //   ReadReg1
  //   ReadReg2
  //   RegData1
  //   RegData2
  //   STR / LDR
  //   ADD / SUB
  //   Stage 2: Instruction Decoding
  //   Stage 3: Execution
  //   ALU Calculation
  //   RegData1
  //   ALUout
  //   Stage 4: Memory Access
  //   ALUout
  //   LDR / STR
  //   ReadDataM
  //   RegDataW
endmodule
